// Logisim project 16_bit_encoder.circ as structural Verilog: 2 circuits, main circuit main
module main (
  input  A,
  input  B,
  input  C,
  input  D,
  input  E,
  input  F,
  input  G,
  input  H,
  input  I,
  input  J,
  input  K,
  input  L,
  input  M,
  input  N,
  input  O,
  input  P
);

  wire decoder_e, decoder_f, decoder_g, decoder_h, decoder_i, decoder_j, decoder_k, or_1_out, or_2_out,
       or_3_out, or_4_out, or_5_out;

  or or_1 (or_1_out, P, B, J, F, D, H, L, N);
  or or_2 (or_2_out, C, D, G, H, L, P, O, K);
  or or_3 (or_3_out, E, H, F, G, N, M, O, P);
  or or_4 (or_4_out, P, I, J, K, L, M, N, O);
  or or_5 (or_5_out, A, or_1_out, or_2_out, or_3_out, or_4_out);
  display_decoder_my decoder (
    .A(or_1_out), .B(or_2_out), .C(or_3_out), .D(or_4_out), .EN(or_5_out), .E(decoder_e), .I(decoder_i),
    .J(decoder_j), .F(decoder_f), .K(decoder_k), .G(decoder_g), .H(decoder_h));
  _7_Segment_Display u_7_segment_display_1 (
    .g(decoder_e), .f(decoder_f), .a(decoder_g), .b(decoder_h), .e(decoder_i), .d(decoder_j), .c(decoder_k));  // open: dp
endmodule

module display_decoder_my (
  input  A,
  input  EN,
  input  B,
  input  C,
  input  D,
  output E,
  output F,
  output G,
  output H,
  output I,
  output J,
  output K
);

  wire decoder_1_out0, decoder_1_out1, decoder_1_out2, decoder_1_out3, decoder_1_out4, decoder_1_out5,
       decoder_1_out6, decoder_1_out7, decoder_1_out8, decoder_1_out9, decoder_1_out10, decoder_1_out11,
       decoder_1_out12, decoder_1_out13, decoder_1_out14, decoder_1_out15, or_1_out, or_2_out, or_3_out,
       or_6_out, or_9_out, or_13_out, or_14_out;

  or or_1 (or_1_out, decoder_1_out8, decoder_1_out6, decoder_1_out5, decoder_1_out3, decoder_1_out2, decoder_1_out0, decoder_1_out9);
  or or_2 (or_2_out, decoder_1_out8, decoder_1_out6, decoder_1_out2, decoder_1_out0);
  Decoder #(.select(4)) decoder_1 (
    .out0(decoder_1_out0), .out1(decoder_1_out1), .out2(decoder_1_out2), .out3(decoder_1_out3),
    .out4(decoder_1_out4), .out5(decoder_1_out5), .out6(decoder_1_out6), .out7(decoder_1_out7),
    .out8(decoder_1_out8), .out9(decoder_1_out9), .out10(decoder_1_out10), .out11(decoder_1_out11),
    .out12(decoder_1_out12), .out13(decoder_1_out13), .out14(decoder_1_out14), .out15(decoder_1_out15),
    .sel({D, C, B, A}), .en(EN));
  or or_3 (or_3_out, decoder_1_out9, decoder_1_out8, decoder_1_out6, decoder_1_out5, decoder_1_out4, decoder_1_out2, decoder_1_out3);
  or or_4 (E, or_3_out, decoder_1_out10, decoder_1_out11, decoder_1_out13, decoder_1_out14, decoder_1_out15);
  or or_5 (I, or_2_out, decoder_1_out10, decoder_1_out11, decoder_1_out12, decoder_1_out13, decoder_1_out14, decoder_1_out15);
  or or_6 (or_6_out, decoder_1_out4, decoder_1_out5, decoder_1_out6, decoder_1_out8, decoder_1_out9, decoder_1_out0);
  or or_7 (F, or_6_out, decoder_1_out10, decoder_1_out11, decoder_1_out12, decoder_1_out14, decoder_1_out15);
  or or_8 (J, or_1_out, decoder_1_out11, decoder_1_out12, decoder_1_out13, decoder_1_out14);
  or or_9 (or_9_out, decoder_1_out0, decoder_1_out2, decoder_1_out3, decoder_1_out5, decoder_1_out6, decoder_1_out7, decoder_1_out8, decoder_1_out9);
  or or_10 (G, or_9_out, decoder_1_out10, decoder_1_out12, decoder_1_out14, decoder_1_out15);
  or or_11 (H, or_13_out, decoder_1_out10, decoder_1_out13);
  or or_12 (K, decoder_1_out10, decoder_1_out11, decoder_1_out13, or_14_out);
  or or_13 (or_13_out, decoder_1_out0, decoder_1_out1, decoder_1_out2, decoder_1_out3, decoder_1_out4, decoder_1_out7, decoder_1_out8, decoder_1_out9);
  or or_14 (or_14_out, decoder_1_out0, decoder_1_out1, decoder_1_out3, decoder_1_out4, decoder_1_out5, decoder_1_out6, decoder_1_out7, decoder_1_out8, decoder_1_out9);
endmodule
