// Logisim project 2-4-decoder.circ as structural Verilog
module decoder_2To4 (
  input  A,
  input  B,
  output Y0,
  output Y1,
  output Y2,
  output Y3
);

  wire not_1_out, not_2_out;

  not not_1 (not_1_out, B);
  not not_2 (not_2_out, A);
  nor nor_1 (Y0, A, B);
  nor nor_2 (Y1, A, not_1_out);
  nor nor_3 (Y2, not_2_out, B);
  and and_1 (Y3, A, B);
endmodule
