// Logisim project 4_bit_pre_encoder.circ as structural Verilog: 1 circuit, main circuit main
module main (
  input  A3,
  input  A2,
  input  A1,
  input  A0,
  output Y1,
  output Y0,
  output V
);

  wire and_1_out, not_1_out;

  not not_1 (not_1_out, A2);
  or or_1 (V, A2, A1, A3, A0);
  or or_2 (Y1, A2, A3);
  and and_1 (and_1_out, not_1_out, A1);
  or or_3 (Y0, and_1_out, A3);
endmodule
