// Logisim project decoder.circ as structural Verilog
// dc_2-4
module decoder_2To4 (
  input  A,
  input  B,
  output Y0,
  output Y1,
  output Y2,
  output Y3
);

  wire not_1_out, not_2_out;

  not not_1 (not_1_out, B);
  not not_2 (not_2_out, A);
  nor nor_1 (Y0, A, B);
  nor nor_2 (Y1, A, not_1_out);
  nor nor_3 (Y2, not_2_out, B);
  and and_1 (Y3, A, B);
endmodule

module decoder_3To8 (
  input  A,
  input  B,
  input  C,
  output Y0,
  output Y1,
  output Y2,
  output Y3,
  output Y4,
  output Y5,
  output Y6,
  output Y7
);

  wire dc1_y0, dc1_y1, dc1_y2, dc1_y3, not_1_out, not_2_out, not_3_out, not_4_out, not_5_out;

  decoder_2To4 dc1 (.A(A), .B(B), .Y0(dc1_y0), .Y1(dc1_y1), .Y2(dc1_y2), .Y3(dc1_y3));
  not not_1 (not_1_out, dc1_y3);
  not not_2 (not_2_out, dc1_y0);
  not not_3 (not_3_out, dc1_y1);
  not not_4 (not_4_out, dc1_y2);
  not not_5 (not_5_out, C);
  nor nor_1 (Y0, not_2_out, C);
  nor nor_2 (Y1, not_2_out, not_5_out);
  nor nor_3 (Y2, C, not_3_out);
  nor nor_4 (Y3, not_5_out, not_3_out);
  nor nor_5 (Y4, not_4_out, C);
  nor nor_6 (Y5, not_4_out, not_5_out);
  nor nor_7 (Y6, not_1_out, C);
  nor nor_8 (Y7, not_1_out, not_5_out);
endmodule
