// Logisim project display_decoder_10.circ as structural Verilog
module display_decoder (
  input  A,
  input  B,
  input  C,
  input  D
);

  wire decoder_1_out0, decoder_1_out1, decoder_1_out2, decoder_1_out3, decoder_1_out4, decoder_1_out5,
       decoder_1_out6, decoder_1_out7, decoder_1_out8, decoder_1_out9, or_1_out, or_2_out, or_3_out,
       or_4_out, or_5_out, or_6_out, or_7_out;

  or or_1 (or_1_out, decoder_1_out8, decoder_1_out6, decoder_1_out5, decoder_1_out3, decoder_1_out2, decoder_1_out0, decoder_1_out9);
  or or_2 (or_2_out, decoder_1_out8, decoder_1_out6, decoder_1_out2, decoder_1_out0);
  Decoder #(.select(4)) decoder_1 (
    .out0(decoder_1_out0), .out1(decoder_1_out1), .out2(decoder_1_out2), .out3(decoder_1_out3),
    .out4(decoder_1_out4), .out5(decoder_1_out5), .out6(decoder_1_out6), .out7(decoder_1_out7),
    .out8(decoder_1_out8), .out9(decoder_1_out9), .sel({D, C, B, A}), .en(1'b1));  // open: out10, out11, out12, out13, out14, out15
  or or_3 (or_3_out, decoder_1_out9, decoder_1_out8, decoder_1_out6, decoder_1_out5, decoder_1_out4, decoder_1_out2, decoder_1_out3);
  or or_4 (or_4_out, decoder_1_out4, decoder_1_out5, decoder_1_out6, decoder_1_out8, decoder_1_out9, decoder_1_out0);
  _7_Segment_Display DD (
    .g(or_3_out), .f(or_4_out), .a(or_5_out), .b(or_6_out), .e(or_2_out), .d(or_1_out), .c(or_7_out));  // open: dp
  or or_5 (or_5_out, decoder_1_out0, decoder_1_out2, decoder_1_out3, decoder_1_out5, decoder_1_out6, decoder_1_out7, decoder_1_out8, decoder_1_out9);
  or or_6 (or_6_out, decoder_1_out0, decoder_1_out1, decoder_1_out2, decoder_1_out3, decoder_1_out4, decoder_1_out7, decoder_1_out8, decoder_1_out9);
  or or_7 (or_7_out, decoder_1_out0, decoder_1_out1, decoder_1_out3, decoder_1_out4, decoder_1_out5, decoder_1_out6, decoder_1_out7, decoder_1_out8, decoder_1_out9);
endmodule
