// Logisim project display_decoder_14.circ as structural Verilog
module display_decoder (
  input  A,
  input  B,
  input  C,
  input  D
);

  wire decoder_1_out0, decoder_1_out1, decoder_1_out2, decoder_1_out3, decoder_1_out4, decoder_1_out5,
       decoder_1_out6, decoder_1_out7, decoder_1_out8, decoder_1_out9, decoder_1_out10, decoder_1_out11,
       decoder_1_out12, decoder_1_out13, decoder_1_out14, decoder_1_out15, or_1_out, or_2_out, or_3_out,
       or_4_out, or_5_out, or_6_out, or_7_out, or_8_out, or_9_out, or_10_out, or_11_out, or_12_out,
       or_13_out, or_14_out;

  or or_1 (or_1_out, decoder_1_out8, decoder_1_out6, decoder_1_out5, decoder_1_out3, decoder_1_out2, decoder_1_out0, decoder_1_out9);
  or or_2 (or_2_out, decoder_1_out8, decoder_1_out6, decoder_1_out2, decoder_1_out0);
  Decoder #(.select(4)) decoder_1 (
    .out0(decoder_1_out0), .out1(decoder_1_out1), .out2(decoder_1_out2), .out3(decoder_1_out3),
    .out4(decoder_1_out4), .out5(decoder_1_out5), .out6(decoder_1_out6), .out7(decoder_1_out7),
    .out8(decoder_1_out8), .out9(decoder_1_out9), .out10(decoder_1_out10), .out11(decoder_1_out11),
    .out12(decoder_1_out12), .out13(decoder_1_out13), .out14(decoder_1_out14), .out15(decoder_1_out15),
    .sel({D, C, B, A}), .en(1'b1));
  or or_3 (or_3_out, decoder_1_out9, decoder_1_out8, decoder_1_out6, decoder_1_out5, decoder_1_out4, decoder_1_out2, decoder_1_out3);
  or or_4 (or_4_out, or_3_out, decoder_1_out10, decoder_1_out11, decoder_1_out13, decoder_1_out14, decoder_1_out15);
  or or_5 (or_5_out, or_2_out, decoder_1_out10, decoder_1_out11, decoder_1_out12, decoder_1_out13, decoder_1_out14, decoder_1_out15);
  or or_6 (or_6_out, decoder_1_out4, decoder_1_out5, decoder_1_out6, decoder_1_out8, decoder_1_out9, decoder_1_out0);
  or or_7 (or_7_out, or_6_out, decoder_1_out10, decoder_1_out11, decoder_1_out12, decoder_1_out14, decoder_1_out15);
  _7_Segment_Display DD (
    .g(or_4_out), .f(or_7_out), .a(or_10_out), .b(or_11_out), .e(or_5_out), .d(or_8_out), .c(or_12_out));  // open: dp
  or or_8 (or_8_out, or_1_out, decoder_1_out11, decoder_1_out12, decoder_1_out13, decoder_1_out14);
  or or_9 (or_9_out, decoder_1_out0, decoder_1_out2, decoder_1_out3, decoder_1_out5, decoder_1_out6, decoder_1_out7, decoder_1_out8, decoder_1_out9);
  or or_10 (or_10_out, or_9_out, decoder_1_out10, decoder_1_out12, decoder_1_out14, decoder_1_out15);
  or or_11 (or_11_out, or_13_out, decoder_1_out10, decoder_1_out13);
  or or_12 (or_12_out, decoder_1_out10, decoder_1_out11, decoder_1_out13, or_14_out);
  or or_13 (or_13_out, decoder_1_out0, decoder_1_out1, decoder_1_out2, decoder_1_out3, decoder_1_out4, decoder_1_out7, decoder_1_out8, decoder_1_out9);
  or or_14 (or_14_out, decoder_1_out0, decoder_1_out1, decoder_1_out3, decoder_1_out4, decoder_1_out5, decoder_1_out6, decoder_1_out7, decoder_1_out8, decoder_1_out9);
endmodule
