// Logisim project xor.circ as structural Verilog: 1 circuit, main circuit main
module main (
  input  A,
  input  B,
  output Y
);

  wire nand_1_out, nand_2_out, not_1_out, not_2_out;

  nand nand_1 (nand_1_out, A, not_1_out);
  not not_1 (not_1_out, B);
  not not_2 (not_2_out, A);
  nand nand_2 (nand_2_out, not_2_out, B);
  nand nand_3 (Y, nand_1_out, nand_2_out);
endmodule
